# Fritzing sketch Schematic (saved by Fritzing 0.9.3b)
breadboards: 1

parts:
  Slave = Arduino Uno (Rev3) - ICSP
  Master = Arduino Uno (Rev3) - ICSP
  part = RFID-RC522
  J1 = Piezo Speaker
  Switch_One = Pushbutton [package="[THT]"]
  Switch_Two = Pushbutton [package="[THT]"]
  J2 = Basic Servo
  part_2 = Basic Servo
  R1 = Resistor [tolerance=±5% resistance=10k package="0603 [SMD]"]
  R2 = Resistor [tolerance=±5% resistance=10k package="0603 [SMD]"]
  Switch_Resistors = KENT_LCD_CONN [package=ffc_16]
  part_3 = Bluetooth HC-05 Macho
  part_4 = Bluetooth HC-05 Macho
  part_5 = Bluetooth HC-05 Macho
  U1 = RELAY [package=relay-t9a-2]

nets:
  N1: Slave.A0, part_2.pulse
  VCC: Slave.5V, part_2.vcc, part_4.VCC, U1.COIL1
  GND: Slave.GND, part_2.gnd, part_4.GROUND
  N2: Slave.D2, part_4.TXD
  N3: Slave.D3_PWM, part_4.RXD
  N4: Slave.D5_PWM, U1.COIL2
  N5: Master.A0, J1.pin1
  GND_2: Master.GND, J1.pin2, Switch_One.Pin_1, Switch_One.Pin_2, J2.gnd, Switch_Resistors.GND, part_3.GROUND
  VCC_2: Master.5V, J2.vcc, R1.Pin_0, R2.Pin_0, Switch_Resistors.+5V, Switch_Resistors.BL, part_3.VCC
  N6: Master.ICSP2_SCK, Switch_Resistors.SCK
  N7: Master.ICSP2_MOSI, Switch_Resistors.MOSI
  N8: Master.D8, Switch_Resistors.CS-LD
  N9: Master.D9_PWM, part.SDA
  N10: Master.D10_PWM/SS, part.GND
  N11: Master.D11_PWM/MOSI, part.MOSI
  N12: Master.D12/MISO, part.MISO
  N13: Master.D13/SCK, part.SCK
  N14: Master.A5/SCL, J2.pulse
  N15: Master.D2, Switch_One.Pin_3, Switch_One.Pin_4, R2.Pin_1
  N16: Master.D3_PWM, Switch_Two.Pin_3, Switch_Two.Pin_4, R1.Pin_1
  N17: Master.D4, part_3.TXD
  N18: Master.D5_PWM, part_3.RXD
  N19: Master.D6_PWM, Switch_Resistors.RESET
  N20: Master.D7, Switch_Resistors.D/C-LD
  3V3: Master.3V3, part.3.3V
  N21: part_5.+6V#12, U1.NO
  N22: part_5.+6V#13, U1.MAIN

notes:
  RFID Door Lock System, Systems Architecture 1 - Coursework 2

custom parts:
  KENT_LCD_CONN: Connector for Kent display (LCD-09560)
